// Logisim project 1_circuito_1.circ as structural Verilog: 1 circuit, main circuit main
module main (
  input  A,
  input  B,
  output F,
  output G
);

  wire and_1_out, and_2_out, and_3_out;

  and and_1 (and_1_out, ~A, ~B);  // AND_Gate
  and and_2 (and_2_out, ~A, B);  // AND_Gate
  and and_3 (and_3_out, A, B);
  or or_1 (G, ~A, B);  // OR_Gate
  or or_2 (F, and_1_out, and_2_out, and_3_out);

  // Notes on the sheet:
  //   A B F
  //   0 0 1
  //   0 1 1
  //   1 0 0
  //   1 1 1
  //   F = A'B' + A'B + AB
  //   Mi primer circuito
  //   G = A' + B
endmodule
