// Logisim project 1_circuito_6.circ as structural Verilog: 1 circuit, main circuit main
module main (
  input  A,
  input  B,
  input  C,
  output D,
  output E,
  output F
);

  wire and_1_out, and_2_out, and_3_out;

  or or_1 (D, A, B, C);
  and and_1 (and_1_out, ~A, B, C);  // AND_Gate
  and and_2 (and_2_out, A, ~B, C);  // AND_Gate
  and and_3 (and_3_out, A, B, ~C);  // AND_Gate
  and and_4 (F, A, B, C);
  or or_2 (E, and_1_out, and_2_out, and_3_out);
endmodule
