// Logisim project 1_circuito_neg_neg.circ as structural Verilog: 1 circuit, main circuit main
module main (
  input  A,
  output F
);

  wire not_1_out;

  not not_1 (not_1_out, A);
  not not_2 (F, not_1_out);
endmodule
