// Logisim project 1_decodificador_1_2.circ as structural Verilog: 1 circuit, main circuit main
module main (
  input  A,
  output S0,
  output S1
);

  not not_1 (S0, A);

  assign S1 = A;

  // Notes on the sheet:
  //   Decodificador de 1 a 2
endmodule
