// Logisim project 1_decodificador_2_4.circ as structural Verilog: 1 circuit, main circuit main
module main (
  input  A1,
  input  A0,
  output S0,
  output S1,
  output S2,
  output S3
);

  and and_1 (S0, ~A1, ~A0);  // AND_Gate
  and and_2 (S1, ~A1, A0);  // AND_Gate
  and and_3 (S2, A1, ~A0);  // AND_Gate
  and and_4 (S3, A1, A0);

  // Notes on the sheet:
  //   Decodificador de 2 a 4
endmodule
