// Logisim project 1_encoder.circ as structural Verilog: 1 circuit, main circuit main
module main (
  input  S3,
  input  S2,
  input  S1,
  input  S0,
  output A1,
  output A0
);

  wire and_1_out, and_2_out, and_3_out, and_4_out;

  and and_1 (and_1_out, ~S3, S2, ~S1, ~S0);  // AND_Gate
  and and_2 (and_2_out, S3, ~S2, ~S1, ~S0);  // AND_Gate
  and and_3 (and_3_out, ~S3, ~S2, S1, ~S0);  // AND_Gate
  and and_4 (and_4_out, S3, ~S2, ~S1, ~S0);  // AND_Gate
  or or_1 (A1, and_1_out, and_2_out);
  or or_2 (A0, and_3_out, and_4_out);
endmodule
