// Logisim project 1_maxiterminos.circ as structural Verilog: 1 circuit, main circuit main
module main (
  input  A,
  input  B,
  input  C,
  output F
);

  wire or_1_out, or_2_out, or_3_out, or_4_out, or_5_out;

  or or_1 (or_1_out, A, B, C);
  or or_2 (or_2_out, A, B, ~C);  // OR_Gate
  or or_3 (or_3_out, A, ~B, C);  // OR_Gate
  or or_4 (or_4_out, ~A, ~B, C);  // OR_Gate
  or or_5 (or_5_out, ~A, ~B, ~C);  // OR_Gate
  and and_1 (F, or_1_out, or_2_out, or_3_out, or_4_out, or_5_out);

  // Notes on the sheet:
  //   F = M0 M1 M2 M6 M7
  //   F = (A+B+C) (A+B+C') (A+B'+C) (A'+B'+C) (A'+B'+C') 
endmodule
