// Logisim project 1_priority_encoder.circ as structural Verilog: 1 circuit, main circuit main
module main (
  input  S3,
  input  S2,
  input  S1,
  input  S0,
  output A1,
  output A0,
  output V
);

  wire and_1_out, and_2_out;

  and and_1 (and_1_out, ~S3, S2);  // AND_Gate
  and and_2 (and_2_out, ~S3, ~S2, S1);  // AND_Gate
  or or_1 (A1, and_1_out, S3);
  or or_2 (A0, and_2_out, S3);
  or or_3 (V, S3, S2, S1, S0);
endmodule
