// Logisim project 2_demultiplexor.circ as structural Verilog: 1 circuit, main circuit main
module main (
  input  E,
  input  Se,
  output S0,
  output S1
);

  and and_1 (S0, E, ~Se);  // AND_Gate
  and and_2 (S1, E, Se);

  // Notes on the sheet:
  //   S0 = ESe'
  //   S1 = ESe
endmodule
