// Logisim project 2_multiplexor.circ as structural Verilog: 1 circuit, main circuit main
module main (
  input  Se,
  input  E1,
  input  E0,
  input  PE1,
  input  PSe,
  input  PE0,
  output Sa,
  output PSa
);

  wire and_1_out, and_2_out, and_3_out, and_4_out, and_5_out, and_6_out;

  and and_1 (and_1_out, PE1, PSe);
  and and_2 (and_2_out, ~PSe, PE0);  // AND_Gate
  and and_3 (and_3_out, ~Se, ~E1, E0);  // AND_Gate
  and and_4 (and_4_out, ~Se, E1, E0);  // AND_Gate
  and and_5 (and_5_out, Se, E1, ~E0);  // AND_Gate
  and and_6 (and_6_out, Se, E1, E0);
  or or_1 (PSa, and_1_out, and_2_out);
  or or_2 (Sa, and_3_out, and_4_out, and_5_out, and_6_out);

  // Notes on the sheet:
  //   Sa = m1+m3+m6+m7
  //   Sa = Se'E1'E0 + Se'E1E0 + SeE1E0' +SeE1E0
endmodule
