// Logisim project 3_ROM.circ as structural Verilog: 1 circuit, main circuit main
module main (
  input  A1,
  input  A0,
  output S4,
  output S3,
  output S2,
  output S1,
  output S0
);

  wire and_1_out, and_2_out, and_3_out, and_4_out;

  and and_1 (and_1_out, ~A1, ~A0);  // AND_Gate
  and and_2 (and_2_out, ~A1, A0);  // AND_Gate
  and and_3 (and_3_out, A1, ~A0);  // AND_Gate
  and and_4 (and_4_out, A1, A0);
  or or_1 (S4, and_3_out, and_4_out);
  or or_2 (S3, and_1_out, and_3_out, and_4_out);
  or or_3 (S2, and_1_out, and_2_out, and_4_out);
  buf or_4 (S1, and_3_out);  // OR_Gate
  or or_5 (S0, and_2_out, and_3_out);

  // Notes on the sheet:
  //   Decodificador de 2 a 4
  //   01100
  //   00101
  //   11011
  //   11100
endmodule
