// Logisim project 3_contador_ripple.circ as structural Verilog: 1 circuit, main circuit main
module main (
  output S1,
  output S0
);

  wire clock_1_out, t_ff_1_qn;

  Clock clock_1 (.out(clock_1_out));
  T_Flip_Flop t_ff_1 (.T(1'b1), .clk(clock_1_out), .Q(S0), .Qn(t_ff_1_qn));  // open: reset, preset
  T_Flip_Flop t_ff_2 (.T(1'b1), .clk(t_ff_1_qn), .Q(S1));  // open: Qn, reset, preset
endmodule
