// Logisim project 3_flip_flop_D.circ as structural Verilog: 1 circuit, main circuit main
module main (
  input  D,
  output Q,
  output No_Q
);

  wire and_1_out, and_2_out, reloj_out;

  Clock reloj (.out(reloj_out));
  and and_1 (and_1_out, ~D, reloj_out);  // AND_Gate
  and and_2 (and_2_out, reloj_out, D);
  nor nor_1 (Q, and_1_out, No_Q);
  nor nor_2 (No_Q, Q, and_2_out);
endmodule
