// Logisim project 3_flip_flop_SR.circ as structural Verilog: 1 circuit, main circuit main
module main (
  input  R,
  input  S,
  output Q,
  output No_Q
);

  wire and_1_out, and_2_out, reloj_out;

  Clock reloj (.out(reloj_out));
  and and_1 (and_1_out, R, reloj_out);
  and and_2 (and_2_out, reloj_out, S);
  nor nor_1 (Q, and_1_out, No_Q);
  nor nor_2 (No_Q, Q, and_2_out);
endmodule
