// Logisim project 3_latch_SR.circ as structural Verilog: 1 circuit, main circuit main
module main (
  input  R,
  input  S,
  output Q,
  output No_Q
);

  nor nor_1 (Q, R, No_Q);
  nor nor_2 (No_Q, Q, S);
endmodule
