// Logisim project 3_registro.circ as structural Verilog: 1 circuit, main circuit main
module main (
  input  D3,
  input  D2,
  input  D1,
  input  D0,
  input  Reset,
  output Q3,
  output Q2,
  output Q1,
  output Q0
);

  wire Reloj_out;

  Clock Reloj (.out(Reloj_out));
  D_Flip_Flop d_ff_1 (.D(D3), .clk(Reloj_out), .Q(Q3), .reset(Reset));  // open: Qn, preset
  D_Flip_Flop d_ff_2 (.D(D2), .clk(Reloj_out), .Q(Q2), .reset(Reset));  // open: Qn, preset
  D_Flip_Flop d_ff_3 (.D(D1), .clk(Reloj_out), .Q(Q1), .reset(Reset));  // open: Qn, preset
  D_Flip_Flop d_ff_4 (.D(D0), .clk(Reloj_out), .Q(Q0), .reset(Reset));  // open: Qn, preset
endmodule
