// Logisim project 3_registro_desplazamiento.circ as structural Verilog: 1 circuit, main circuit main
module main (
  input  E,
  input  Reset,
  output S
);

  wire d_ff_1_q, d_ff_2_q, d_ff_3_q, Reloj_out;

  Clock Reloj (.out(Reloj_out));
  D_Flip_Flop d_ff_1 (.D(E), .clk(Reloj_out), .Q(d_ff_1_q), .reset(Reset));  // open: Qn, preset
  D_Flip_Flop d_ff_2 (.D(d_ff_1_q), .clk(Reloj_out), .Q(d_ff_2_q), .reset(Reset));  // open: Qn, preset
  D_Flip_Flop d_ff_3 (.D(d_ff_2_q), .clk(Reloj_out), .Q(d_ff_3_q), .reset(Reset));  // open: Qn, preset
  D_Flip_Flop d_ff_4 (.D(d_ff_3_q), .clk(Reloj_out), .Q(S), .reset(Reset));  // open: Qn, preset
endmodule
