// Logisim project 4_comparador.circ as structural Verilog: 3 circuits, main circuit main
module main (
);

  comparador_4bits comparador_4bits_1 ();  // open: A, B, Igual, Menor, Mayor
endmodule

module Comparador_1bit (
  input  A,
  input  B,
  output Igual,
  output mayor
);

  xnor xnor_1 (Igual, A, B);
  and and_1 (mayor, A, ~B);  // AND_Gate
endmodule

module comparador_4bits (
  input  [3:0] A,
  input  [3:0] B,
  output Igual,
  output Menor,
  output Mayor
);

  wire and_1_out, and_2_out, and_3_out, comparador_1bit_1_igual, comparador_1bit_1_mayor,
       comparador_1bit_2_igual, comparador_1bit_2_mayor, comparador_1bit_3_igual, comparador_1bit_3_mayor,
       comparador_1bit_4_igual, comparador_1bit_4_mayor;

  Comparador_1bit comparador_1bit_1 (
    .A(A[0]), .B(B[0]), .Igual(comparador_1bit_1_igual), .mayor(comparador_1bit_1_mayor));
  Comparador_1bit comparador_1bit_2 (
    .A(A[1]), .B(B[1]), .Igual(comparador_1bit_2_igual), .mayor(comparador_1bit_2_mayor));
  Comparador_1bit comparador_1bit_3 (
    .A(A[2]), .B(B[2]), .Igual(comparador_1bit_3_igual), .mayor(comparador_1bit_3_mayor));
  Comparador_1bit comparador_1bit_4 (
    .A(A[3]), .B(B[3]), .Igual(comparador_1bit_4_igual), .mayor(comparador_1bit_4_mayor));
  and and_1 (and_1_out, comparador_1bit_1_mayor, comparador_1bit_2_igual, comparador_1bit_3_igual, comparador_1bit_4_igual);
  and and_2 (and_2_out, comparador_1bit_2_mayor, comparador_1bit_3_igual, comparador_1bit_4_igual);
  and and_3 (and_3_out, comparador_1bit_3_mayor, comparador_1bit_4_igual);
  and and_4 (Igual, comparador_1bit_1_igual, comparador_1bit_2_igual, comparador_1bit_3_igual, comparador_1bit_4_igual);
  and and_5 (Menor, ~Igual, ~Mayor);  // AND_Gate
  or or_1 (Mayor, and_1_out, and_2_out, and_3_out, comparador_1bit_4_mayor);
endmodule
